# Fritzing sketch bike_air_quality_sensors_damien (saved by Fritzing 0.9.2b)
breadboards: 3

parts:
  RHT2 = Humidity and Temperature Sensor RHT03
  Part4 = Bluetooth Module Breakout - Roving Networks (RN-41)  # not connected
  C4 = Electrolytic Capacitor [capacitance=0.47mF voltage=16V package="100 mil [THT, electrolytic]"]
  Part5 = Gas Sensor Breakout Board
  Q1 = PNP-Transistor [package="TO92 [THT]"]
  R4 = Resistor [tolerance=±5% resistance=220 package="0603 [SMD]"]
  Part6 = Arduino Uno (Rev3)
  R5 = Resistor [tolerance=±5% resistance=220 package="0603 [SMD]"]
  R6 = Resistor [tolerance=±5% resistance=220 package="0603 [SMD]"]

nets:
  GND: RHT2.GND_1, RHT2.GND_2, C4.+, Part5.GND, Part6.GND
  N1: C4.-, R4.Pin_1
  N2: Part5.A1, Part5.A2, Part6.A0, R6.Pin_0
  N3: Part5.B1, Part5.B2, Q1.C, R4.Pin_0, Part6.5V, R6.Pin_1
  N4: Part5.H1, Q1.E
  N5: Q1.B, R5.Pin_0
  N6: Part6.D3_PWM, R5.Pin_1
